# Fritzing sketch flood_magnet_controller (saved by Fritzing 0.9.6b)
breadboards: 1

parts:
  Part1 = Arduino Nano 33 IOT
  OLED1 = WaveShare 1.3 inch OLED
  S1 = Pushbutton [package="[THT]"]
  S2 = Pushbutton [package="[THT]"]
  S3 = Pushbutton [package="[THT]"]
  R1 = Resistor [tolerance=±5% resistance=10k power=0.25 package=THT]
  S4 = Pushbutton [package="[THT]"]
  S5 = Pushbutton [package="[THT]"]
  S6 = Pushbutton [package="[THT]"]
  S7 = Pushbutton [package="[THT]"]
  R2 = Resistor [tolerance=±5% resistance=10k power=0.25 package=THT]
  R3 = Resistor [tolerance=±5% resistance=10k power=0.25 package=THT]
  R4 = Resistor [tolerance=±5% resistance=10k power=0.25 package=THT]
  R5 = Resistor [tolerance=±5% resistance=10k power=0.25 package=THT]
  R6 = Resistor [tolerance=±5% resistance=10k power=0.25 package=THT]
  LED1 = LED - 5mm [color="Red (633nm)" current=0.030 package="5 mm [THT]"]
  LED2 = LED - 5mm [color="Yellow (595nm)" current=0.030 package="5 mm [THT]"]
  LED3 = LED - 5mm [color="Green (570nm)" current=0.030 package="5 mm [THT]"]
  R7 = Resistor [tolerance=±5% resistance=270 power=0.25 package=THT]
  R8 = Resistor [tolerance=±5% resistance=270 power=0.25 package=THT]
  R9 = Resistor [tolerance=±5% resistance=270 power=0.25 package=THT]
  R10 = Resistor [tolerance=±5% resistance=270 power=0.25 package=THT]
  R11 = Resistor [tolerance=±5% resistance=270 power=0.25 package=THT]
  R12 = Resistor [tolerance=±5% resistance=270 power=0.25 package=THT]
  J1 = Piezo Speaker
  J2 = female pin header, 3 pins [form="♀ (female)"]
  LED7 = RGB LED (com. cathode, rgb) [package="5 mm [THT]"]
  U1 = TRANSISTOR_NPN_2 [package=to-92]
  R14 = Resistor [tolerance=±5% resistance=56 power=0.25 package=THT]
  R15 = Resistor [tolerance=±5% resistance=2.2k power=0.25 package=THT]

nets:
  N1: Part1.RX, J2.pin2
  N2: Part1.TX, J2.pin3
  N3: Part1.RESET, Part1.A7, S3.Pin_1, S3.Pin_2, R1.Pin_0
  GND: Part1.GND, Part1.D13~, OLED1.DIN, OLED1.GND, S1.Pin_3, S1.Pin_4, S2.Pin_3, S2.Pin_4, S3.Pin_3, S3.Pin_4, S4.Pin_3, S4.Pin_4, S5.Pin_3, S5.Pin_4, S6.Pin_3, S6.Pin_4, S7.Pin_3, S7.Pin_4, LED1.cathode, LED2.cathode, LED3.cathode, J2.pin1, LED7.common_cathode, U1.E
  N4: Part1.D2, R11.Pin_1
  N5: Part1.D3~, R10.Pin_1
  N6: Part1.D4, OLED1.RES
  N7: Part1.D5~, R12.Pin_1
  N8: Part1.D6~, R7.Pin_1
  N9: Part1.D7, OLED1.CS
  N10: Part1.D8, OLED1.CLK
  N11: Part1.D9~, R8.Pin_1
  N12: Part1.D10~, R9.Pin_1
  N13: Part1.D11/MOSI, Part1.+5V, OLED1.NC
  N14: Part1.A6, S2.Pin_1, S2.Pin_2, R2.Pin_0
  N15: Part1.A5, S4.Pin_1, S4.Pin_2, R3.Pin_0
  N16: Part1.A4, S5.Pin_1, S5.Pin_2, R4.Pin_0
  N17: Part1.A3, S6.Pin_1, S6.Pin_2, R5.Pin_0
  N18: Part1.A2, S7.Pin_1, S7.Pin_2, R6.Pin_0
  N19: Part1.A1, R15.Pin_1
  N20: Part1.A0, OLED1.D/C
  3V3: Part1.3V3, OLED1.VCC, R1.Pin_1, R2.Pin_1, R3.Pin_1, R4.Pin_1, R5.Pin_1, R6.Pin_1, R14.Pin_1
  N21: S1.Pin_1, S1.Pin_2
  N22: LED1.anode, R7.Pin_0
  N23: LED2.anode, R8.Pin_0
  N24: LED3.anode, R9.Pin_0
  N25: R10.Pin_0, LED7.green_anode
  N26: R11.Pin_0, LED7.blue_anode
  N27: R12.Pin_0, LED7.red_anode
  N28: J1.pin1, U1.C
  N29: J1.pin2, R14.Pin_0
  N30: U1.B, R15.Pin_0

notes:
  Nano 33 IoT
  VCC
  GND
  DIN
  CLK
  CS
  DC
  RST
  BUSY
  RESET
  B1 DRY
  B2 RAIN
  B3 FLOOD
  B4 REPLAY / MUTE
  B5 DEMO
  B6 CLK / AP
  3V3
  L3 CLEAR
  L1 WARNING
  L2 ALERT
  RGB LED
  USB POWER ->
  SERIAL
  CBE
  +
  V2.0

custom parts:
  Arduino Nano 33 IOT: The Arduino Nano 33 IoT is the easiest and cheapest point of entry to enhance existing devices (and creating new ones) to be part of the IoT and designing pico-network applications. Whether you are looking at building a sensor network connected to your office or home router, or if you want to create a BLE device sending data to a cellphone, the Nano 33 IoT is your one-stop-solution for many of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
  WaveShare 1.3 inch OLED: 128x64 Monochrom OLED Display with a SH1106 controller
